# Fritzing sketch Fritzing plan of wiring (saved by Fritzing 0.9.3b)
breadboards: 1

parts:
  LCD1 = LCD screen
  HC-SR04_Sensor_1 = HC-SR04 Ultrasonic Distance Sensor
  Part1 = Arduino Uno (Rev3) - ICSP

nets:
  GND: LCD1.VSS, LCD1.R/W, LCD1.LED-, HC-SR04_Sensor_1.GND, Part1.GND
  VDD: LCD1.VDD, HC-SR04_Sensor_1.VCC, Part1.5V
  N1: LCD1.RS, Part1.ICSP_MISO, Part1.D12/MISO
  N2: LCD1.E, Part1.D11_PWM/MOSI
  N3: LCD1.DB4, Part1.D5_PWM
  N4: LCD1.DB5, Part1.D4
  N5: LCD1.DB6, Part1.D3_PWM
  N6: LCD1.DB7, Part1.D2
  N7: LCD1.LED+, Part1.3V3
  N8: HC-SR04_Sensor_1.TRIG, Part1.D9_PWM
  N9: HC-SR04_Sensor_1.ECHO, Part1.D8

// code stored in the sketch: Plan.ino
#include <LiquidCrystal.h>
LiquidCrystal lcd(12, 11, 5, 4, 3, 2);


int trigger = 9;
int echo = 8;
float distance;
float t;


void setup() {
  pinMode(trigger, OUTPUT);
  pinMode(echo, INPUT);
 
 lcd.begin(16, 2);



}

void loop() {
  digitalWrite(trigger, HIGH);
  delay(1);
  digitalWrite(trigger, LOW);
  t = pulseIn(echo, HIGH);
  distance = (t / 2) / 28.9 ;//The 28.9 is what you get from all the calculation to do with temperature.
 
lcd.print(distance);

}
